# Fritzing sketch switch_luz (saved by Fritzing 0.9.2b)
breadboards: 1

parts:
  Part1 = Arduino Uno (Rev3)
  S1 = Pushbutton [package="[THT]"]
  LED2 = smd LED [color="Red (633nm)" package="0603 [SMD]"]
  R2 = Resistor [tolerance=±5% resistance=220 package=THT]
  S2 = Pushbutton [package="[THT]"]
  S3 = Pushbutton [package="[THT]"]
  S4 = Pushbutton [package="[THT]"]
  R4 = Resistor [tolerance=±5% resistance=1k package=THT]
  R5 = Resistor [tolerance=±5% resistance=1k package=THT]
  R6 = Resistor [tolerance=±5% resistance=1k package=THT]
  R7 = Resistor [tolerance=±5% resistance=1k package=THT]
  LED3 = smd LED [color="Red (633nm)" package="0603 [SMD]"]
  LED4 = smd LED [color="Red (633nm)" package="0603 [SMD]"]
  LED5 = smd LED [color="Red (633nm)" package="0603 [SMD]"]
  R8 = Resistor [tolerance=±5% resistance=220 package=THT]
  R9 = Resistor [tolerance=±5% resistance=220 package=THT]
  R10 = Resistor [tolerance=±5% resistance=220 package=THT]

nets:
  N1: Part1.D9_PWM, LED4.anode
  N2: Part1.D10_PWM/SS, LED5.anode, R9.Pin_0
  N3: Part1.D11_PWM/MOSI, LED3.anode
  N4: Part1.D12/MISO, LED2.anode
  N5: Part1.D2, S4.Pin_3, S4.Pin_4, R4.Pin_1
  N6: Part1.D3_PWM, S2.Pin_3, S2.Pin_4, R7.Pin_1
  N7: Part1.D4, S1.Pin_3, S1.Pin_4, R6.Pin_1
  N8: Part1.D5_PWM, S3.Pin_3, S3.Pin_4, R5.Pin_1
  N9: Part1.5V, S3.Pin_1, S3.Pin_2
  N10: Part1.GND, R5.Pin_0
  N11: S1.Pin_1, S1.Pin_2, S2.Pin_1, S2.Pin_2, S4.Pin_1, S4.Pin_2
  N12: LED2.cathode, R2.Pin_0
  N13: R2.Pin_1, R8.Pin_1, R9.Pin_1, R10.Pin_1
  N14: R4.Pin_0, R6.Pin_0, R7.Pin_0
  N15: LED3.cathode, R8.Pin_0
  N16: LED4.cathode, R10.Pin_0
